# Fritzing sketch ConnecteXmasTrees (saved by Fritzing 0.9.3b)
breadboards: 1

parts:
  2N2222 = NPN-Transistor [package="TO92 [THT]"]
  WeMos = WeMos D1 Mini
  Button_or_Motion_Sensor = Pushbutton [package="[THT]"]
  Pull-down_for_button = Resistor [tolerance=±5% resistance=10k package=THT]
  R2 = Resistor [tolerance=±5% resistance=2.2k package=THT]
  R3 = Resistor [tolerance=±5% resistance=2.2k package=THT]
  2N2222_2 = NPN-Transistor [package="TO92 [THT]"]
  TREE_TOP = LED - 5mm [color="Red (633nm)" package="5 mm [THT]"]
  TREE_MAIN = LED - 5mm [color="Green (555nm)" package="5 mm [THT]"]

nets:
  N1: 2N2222.E, WeMos.G, Pull-down_for_button.Pin_1, 2N2222_2.E
  N2: 2N2222.B, R2.Pin_1
  N3: 2N2222.C, TREE_MAIN.cathode
  N4: WeMos.5V, Button_or_Motion_Sensor.Pin_3, Button_or_Motion_Sensor.Pin_4, TREE_TOP.anode, TREE_MAIN.anode
  N5: WeMos.D2, Button_or_Motion_Sensor.Pin_1, Button_or_Motion_Sensor.Pin_2, Pull-down_for_button.Pin_0
  N6: WeMos.D6, R3.Pin_0
  N7: WeMos.D8, R2.Pin_0
  N8: R3.Pin_1, 2N2222_2.B
  N9: 2N2222_2.C, TREE_TOP.cathode
