# Fritzing sketch Pond_filler (saved by Fritzing 0.9.3b)
circuit board: 8.46667cm x 5.64444cm
breadboards: 1

parts:
  Relay = RELAY [package=OJ]
  PN2222a = NPN-Transistor [package="TO92 [THT]"]
  R1_Pullup = Resistor [tolerance=±5% resistance=4.7k package="2010 [SMD]"]
  R2_Pullup = Resistor [tolerance=±5% resistance=4.7k package="2010 [SMD]"]
  1N4001 = Rectifier Diode [package="Melf DO-213 AA [SMD]"]
  Sprinkler_Valve = Screw terminal - 2 pins [package=THT]
  Probes = Screw terminal - 2 pins [package=THT]
  R3 = Resistor [tolerance=±5% resistance=2.2k package="2010 [SMD]"]
  Part1 = Arduino Uno (Rev3) [part_number=IOT2020]

nets:
  N1: Relay.COIL2, R1_Pullup.Pin_1, R2_Pullup.Pin_1, 1N4001.cathode, Part1.5V
  N2: Relay.MAIN, Sprinkler_Valve.pin1
  N3: Relay.NO, Sprinkler_Valve.pin2
  N4: Relay.COIL1, PN2222a.C, 1N4001.anode
  N5: PN2222a.E, Part1.GND
  N6: PN2222a.B, R3.Pin_1
  N7: R1_Pullup.Pin_0, Probes.pin1, Part1.D5_PWM
  N8: R2_Pullup.Pin_0, Probes.pin2, Part1.D6_PWM
  N9: R3.Pin_0, Part1.D7
